// Logisim project 2421 to 7.circ as structural Verilog: 1 circuit, main circuit main
module main (
  input  [3:0] in_1,
  output out_2,
  output out_3,
  output out_4,
  output out_5,
  output out_6,
  output out_7,
  output out_8
);

  wire _0_out, _1_out, _2_out, _3_out, _4_out, _5_out, _6_out, _7_out, _8_out, _9_out, A_prime_B_out,
       AB_prime_out, and_1_out, and_2_out, C_D_out, C_prime_D_prime_out, not_1_out, not_2_out, not_3_out,
       not_4_out, not_5_out, not_6_out, or_1_out, or_2_out;

  not not_1 (not_1_out, in_1[2]);
  not not_2 (not_2_out, in_1[3]);
  not not_3 (not_3_out, in_1[2]);
  not not_4 (not_4_out, in_1[1]);
  not not_5 (not_5_out, in_1[0]);
  not not_6 (not_6_out, in_1[3]);
  nand C_prime_D_prime (C_prime_D_prime_out, in_1[0], in_1[1]);
  and A_prime_B (A_prime_B_out, not_6_out, in_1[2]);
  or C_D (C_D_out, in_1[0], in_1[1]);
  and AB_prime (AB_prime_out, in_1[3], not_1_out);
  and and_1 (and_1_out, A_prime_B_out, C_D_out);
  and and_2 (and_2_out, AB_prime_out, C_prime_D_prime_out);
  or or_1 (or_1_out, and_1_out, and_2_out);
  and _9 (_9_out, in_1[1], in_1[0], in_1[3], in_1[2]);
  and _8 (_8_out, in_1[1], in_1[3], in_1[2], not_5_out);
  and _7 (_7_out, in_1[3], in_1[2], not_4_out, in_1[0]);
  and _6 (_6_out, in_1[3], in_1[2], not_4_out, not_5_out);
  and _5 (_5_out, in_1[1], in_1[3], in_1[0], not_3_out);
  and _4 (_4_out, in_1[2], not_2_out, not_4_out, not_5_out);
  and _3 (_3_out, not_3_out, in_1[1], not_2_out, in_1[0]);
  and _2 (_2_out, not_2_out, not_3_out, in_1[1], not_5_out);
  and _1 (_1_out, not_2_out, not_3_out, in_1[0], not_4_out);
  and _0 (_0_out, not_3_out, not_5_out, not_4_out, not_2_out);
  or or_2 (or_2_out, _0_out, or_1_out);
  or or_3 (out_2, or_2_out, _3_out, _9_out, _8_out, _7_out, _6_out, _5_out, _2_out);
  or or_4 (out_3, _9_out, _6_out, _5_out, _7_out, _8_out, _4_out, or_2_out);
  or or_5 (out_4, _8_out, _6_out, _2_out, or_2_out);
  or or_6 (out_5, _2_out, _9_out, _8_out, _6_out, _5_out, _3_out, or_2_out);
  or or_7 (out_6, _1_out, _4_out, _9_out, _8_out, _7_out, _6_out, _5_out, _3_out, or_2_out);
  or or_8 (out_7, _1_out, _9_out, _8_out, _7_out, _4_out, _3_out, _2_out, or_2_out);
  or or_9 (out_8, _3_out, _9_out, _8_out, _6_out, _5_out, _4_out, _2_out);

  // Notes on the sheet:
  //   = (CD)'
  //   A'B(C+D)
  //   AB'(C'+D')
endmodule
