// Logisim project 2421 가산기.circ as structural Verilog: 1 circuit, main circuit main
module main (
  input  in_1,
  input  in_2,
  input  [3:0] in_3,
  input  [3:0] in_4,
  output out_5,
  output [3:0] out_6
);

  wire and_1_out, and_2_out, and_3_out, and_4_out, and_5_out, and_6_out, nor_1_out, nor_2_out, not_1_out,
       not_3_out, or_1_out, or_2_out, or_3_out;
  wire [2:2] and_7_out, not_2_out;
  wire [3:0] adder_1_out, adder_2_out, multiplexer_1_out, subtractor_1_out;

  Adder #(.width(4)) adder_1 (.a(in_3), .b(in_4), .out(adder_1_out), .cin(in_1), .cout(out_5));
  and and_1 (and_1_out, in_3[3], in_4[3]);
  or or_1 (or_1_out, adder_1_out[0], adder_1_out[1]);
  and and_2 (and_2_out, or_1_out, adder_1_out[2]);
  not not_1 (not_1_out, adder_1_out[3]);
  nor nor_1 (nor_1_out, adder_1_out[2], adder_1_out[1]);
  nor nor_2 (nor_2_out, in_3[3], in_4[3]);
  not not_2 (not_2_out[2], in_2);
  and and_3 (and_3_out, adder_1_out[0], adder_1_out[1]);
  and and_4 (and_4_out, and_2_out, not_1_out);
  and and_5 (and_5_out, adder_1_out[3], nor_1_out);
  or or_2 (or_2_out, and_3_out, adder_1_out[2]);
  or or_3 (or_3_out, and_4_out, and_5_out);
  Multiplexer #(.width(4)) multiplexer_1 (
    .in0(adder_1_out), .in1(subtractor_1_out), .out(multiplexer_1_out), .sel(not_3_out));  // open: en
  Subtractor #(.width(4)) subtractor_1 (
    .a(adder_1_out), .b({in_2, {2{not_2_out[2]}}, in_2}), .out(subtractor_1_out));  // open: bin, bout
  not not_3 (not_3_out, and_6_out);
  and and_6 (and_6_out, or_2_out, adder_1_out[3]);
  and and_7 (and_7_out[2], or_3_out, nor_2_out);
  Adder #(.width(4)) adder_2 (
    .a(adder_1_out), .b({in_2, {2{and_7_out[2]}}, in_2}), .out(adder_2_out));  // open: cin, cout
  Multiplexer #(.width(4)) multiplexer_2 (
    .in0(adder_2_out), .in1(multiplexer_1_out), .out(out_6), .sel(and_1_out));  // open: en

  // Notes on the sheet:
  //   두 수의 MSB가 모두 0일때 1
endmodule
