// Logisim project 2421 병렬가산기.circ as structural Verilog: 1 circuit, main circuit main
module main (
  input  in_1,
  input  [3:0] in_2,
  input  [3:0] in_3,
  input  [3:0] in_4,
  input  [3:0] in_5,
  input  [3:0] in_6,
  input  [3:0] in_7,
  input  [3:0] in_8,
  input  [3:0] in_9,
  output [3:0] out_10,
  output [3:0] out_11,
  output [3:0] out_12,
  output [3:0] out_13,
  output [3:0] out_14
);

  wire main_1_out_5, main_2_out_5, main_3_out_5;

  \_2421_가산기_main  main_1 (.in_3(in_2), .in_4(in_3), .out_6(out_10), .out_5(main_1_out_5), .in_1(in_1), .in_2(in_1));
  \_2421_가산기_main  main_2 (
    .in_3(in_4), .in_4(in_5), .out_6(out_11), .out_5(main_2_out_5), .in_1(main_1_out_5), .in_2(in_1));
  \_2421_가산기_main  main_3 (
    .in_3(in_6), .in_4(in_7), .out_6(out_12), .out_5(main_3_out_5), .in_1(main_2_out_5), .in_2(in_1));
  \_2421_가산기_main  main_4 (
    .in_3(in_8), .in_4(in_9), .out_6(out_13), .out_5(out_14[0]), .in_1(main_3_out_5), .in_2(in_1));

  assign out_14[3:1] = {3{in_1}};
endmodule
