// Logisim project main.circ as structural Verilog: 1 circuit, main circuit main
module main (
  input  [3:0] in_1,
  input  [3:0] in_2,
  input  [3:0] in_3,
  input  [3:0] in_4,
  input  [3:0] in_5,
  input  [3:0] in_6,
  input  [3:0] in_7,
  input  [3:0] in_8,
  input  \무조건_0으로_세트 
);

  wire main_1_out_2, main_1_out_3, main_1_out_4, main_1_out_5, main_1_out_6, main_1_out_7, main_1_out_8,
       main_2_out_2, main_2_out_3, main_2_out_4, main_2_out_5, main_2_out_6, main_2_out_7, main_2_out_8,
       main_3_out_2, main_3_out_3, main_3_out_4, main_3_out_5, main_3_out_6, main_3_out_7, main_3_out_8,
       main_4_out_2, main_4_out_3, main_4_out_4, main_4_out_5, main_4_out_6, main_4_out_7, main_4_out_8,
       main_5_out_2, main_5_out_3, main_5_out_4, main_5_out_5, main_5_out_6, main_5_out_7, main_5_out_8,
       main_6_out_2, main_6_out_3, main_6_out_4, main_6_out_5, main_6_out_6, main_6_out_7, main_6_out_8,
       main_7_out_2, main_7_out_3, main_7_out_4, main_7_out_5, main_7_out_6, main_7_out_7, main_7_out_8,
       main_8_out_2, main_8_out_3, main_8_out_4, main_8_out_5, main_8_out_6, main_8_out_7, main_8_out_8,
       main_9_out_2, main_9_out_3, main_9_out_4, main_9_out_5, main_9_out_6, main_9_out_7, main_9_out_8,
       main_10_out_2, main_10_out_3, main_10_out_4, main_10_out_5, main_10_out_6, main_10_out_7,
       main_10_out_8, main_11_out_2, main_11_out_3, main_11_out_4, main_11_out_5, main_11_out_6,
       main_11_out_7, main_11_out_8, main_12_out_2, main_12_out_3, main_12_out_4, main_12_out_5,
       main_12_out_6, main_12_out_7, main_12_out_8, main_13_out_2, main_13_out_3, main_13_out_4,
       main_13_out_5, main_13_out_6, main_13_out_7, main_13_out_8;
  wire [3:0] \_2421_병렬가산기_out_10 , \_2421_병렬가산기_out_11 , \_2421_병렬가산기_out_12 , \_2421_병렬가산기_out_13 ,
       \_2421_병렬가산기_out_14 ;

  _7_Segment_Display u_7_segment_display_1 (
    .g(main_1_out_8), .f(main_1_out_3), .a(main_1_out_2), .b(main_1_out_7), .e(main_1_out_4),
    .d(main_1_out_5), .c(main_1_out_6));  // open: dp
  _2421_to_7_main main_1 (
    .in_1(in_1), .out_2(main_1_out_2), .out_3(main_1_out_3), .out_4(main_1_out_4), .out_5(main_1_out_5),
    .out_6(main_1_out_6), .out_7(main_1_out_7), .out_8(main_1_out_8));
  _7_Segment_Display u_7_segment_display_2 (
    .g(main_2_out_8), .f(main_2_out_3), .a(main_2_out_2), .b(main_2_out_7), .e(main_2_out_4),
    .d(main_2_out_5), .c(main_2_out_6));  // open: dp
  _2421_to_7_main main_2 (
    .in_1(in_2), .out_2(main_2_out_2), .out_3(main_2_out_3), .out_4(main_2_out_4), .out_5(main_2_out_5),
    .out_6(main_2_out_6), .out_7(main_2_out_7), .out_8(main_2_out_8));
  _2421_to_7_main main_3 (
    .in_1(in_3), .out_2(main_3_out_2), .out_3(main_3_out_3), .out_4(main_3_out_4), .out_5(main_3_out_5),
    .out_6(main_3_out_6), .out_7(main_3_out_7), .out_8(main_3_out_8));
  _7_Segment_Display u_7_segment_display_3 (
    .g(main_3_out_8), .f(main_3_out_3), .a(main_3_out_2), .b(main_3_out_7), .e(main_3_out_4),
    .d(main_3_out_5), .c(main_3_out_6));  // open: dp
  _7_Segment_Display u_7_segment_display_4 (
    .g(main_4_out_8), .f(main_4_out_3), .a(main_4_out_2), .b(main_4_out_7), .e(main_4_out_4),
    .d(main_4_out_5), .c(main_4_out_6));  // open: dp
  _2421_to_7_main main_4 (
    .in_1(\_2421_병렬가산기_out_14 ), .out_2(main_4_out_2), .out_3(main_4_out_3), .out_4(main_4_out_4),
    .out_5(main_4_out_5), .out_6(main_4_out_6), .out_7(main_4_out_7), .out_8(main_4_out_8));
  _7_Segment_Display u_7_segment_display_5 (
    .g(main_5_out_8), .f(main_5_out_3), .a(main_5_out_2), .b(main_5_out_7), .e(main_5_out_4),
    .d(main_5_out_5), .c(main_5_out_6));  // open: dp
  _2421_to_7_main main_5 (
    .in_1(in_4), .out_2(main_5_out_2), .out_3(main_5_out_3), .out_4(main_5_out_4), .out_5(main_5_out_5),
    .out_6(main_5_out_6), .out_7(main_5_out_7), .out_8(main_5_out_8));
  _7_Segment_Display u_7_segment_display_6 (
    .g(main_6_out_8), .f(main_6_out_3), .a(main_6_out_2), .b(main_6_out_7), .e(main_6_out_4),
    .d(main_6_out_5), .c(main_6_out_6));  // open: dp
  _2421_to_7_main main_6 (
    .in_1(\_2421_병렬가산기_out_13 ), .out_2(main_6_out_2), .out_3(main_6_out_3), .out_4(main_6_out_4),
    .out_5(main_6_out_5), .out_6(main_6_out_6), .out_7(main_6_out_7), .out_8(main_6_out_8));
  _2421_to_7_main main_7 (
    .in_1(\_2421_병렬가산기_out_12 ), .out_2(main_7_out_2), .out_3(main_7_out_3), .out_4(main_7_out_4),
    .out_5(main_7_out_5), .out_6(main_7_out_6), .out_7(main_7_out_7), .out_8(main_7_out_8));
  \_2421_병렬가산기_main  \_2421_병렬가산기  (
    .in_2(in_4), .in_3(in_8), .in_4(in_3), .in_5(in_7), .in_6(in_2), .in_7(in_6), .in_8(in_1), .in_9(in_5),
    .out_10(\_2421_병렬가산기_out_10 ), .out_11(\_2421_병렬가산기_out_11 ), .out_12(\_2421_병렬가산기_out_12 ),
    .out_13(\_2421_병렬가산기_out_13 ), .out_14(\_2421_병렬가산기_out_14 ), .in_1(\무조건_0으로_세트 ));
  _7_Segment_Display u_7_segment_display_7 (
    .g(main_7_out_8), .f(main_7_out_3), .a(main_7_out_2), .b(main_7_out_7), .e(main_7_out_4),
    .d(main_7_out_5), .c(main_7_out_6));  // open: dp
  _7_Segment_Display u_7_segment_display_8 (
    .g(main_8_out_8), .f(main_8_out_3), .a(main_8_out_2), .b(main_8_out_7), .e(main_8_out_4),
    .d(main_8_out_5), .c(main_8_out_6));  // open: dp
  _2421_to_7_main main_8 (
    .in_1(in_5), .out_2(main_8_out_2), .out_3(main_8_out_3), .out_4(main_8_out_4), .out_5(main_8_out_5),
    .out_6(main_8_out_6), .out_7(main_8_out_7), .out_8(main_8_out_8));
  _7_Segment_Display u_7_segment_display_9 (
    .g(main_9_out_8), .f(main_9_out_3), .a(main_9_out_2), .b(main_9_out_7), .e(main_9_out_4),
    .d(main_9_out_5), .c(main_9_out_6));  // open: dp
  _2421_to_7_main main_9 (
    .in_1(\_2421_병렬가산기_out_11 ), .out_2(main_9_out_2), .out_3(main_9_out_3), .out_4(main_9_out_4),
    .out_5(main_9_out_5), .out_6(main_9_out_6), .out_7(main_9_out_7), .out_8(main_9_out_8));
  _7_Segment_Display u_7_segment_display_10 (
    .g(main_10_out_8), .f(main_10_out_3), .a(main_10_out_2), .b(main_10_out_7), .e(main_10_out_4),
    .d(main_10_out_5), .c(main_10_out_6));  // open: dp
  _2421_to_7_main main_10 (
    .in_1(in_6), .out_2(main_10_out_2), .out_3(main_10_out_3), .out_4(main_10_out_4), .out_5(main_10_out_5),
    .out_6(main_10_out_6), .out_7(main_10_out_7), .out_8(main_10_out_8));
  _2421_to_7_main main_11 (
    .in_1(\_2421_병렬가산기_out_10 ), .out_2(main_11_out_2), .out_3(main_11_out_3), .out_4(main_11_out_4),
    .out_5(main_11_out_5), .out_6(main_11_out_6), .out_7(main_11_out_7), .out_8(main_11_out_8));
  _7_Segment_Display u_7_segment_display_11 (
    .g(main_11_out_8), .f(main_11_out_3), .a(main_11_out_2), .b(main_11_out_7), .e(main_11_out_4),
    .d(main_11_out_5), .c(main_11_out_6));  // open: dp
  _7_Segment_Display u_7_segment_display_12 (
    .g(main_12_out_8), .f(main_12_out_3), .a(main_12_out_2), .b(main_12_out_7), .e(main_12_out_4),
    .d(main_12_out_5), .c(main_12_out_6));  // open: dp
  _2421_to_7_main main_12 (
    .in_1(in_7), .out_2(main_12_out_2), .out_3(main_12_out_3), .out_4(main_12_out_4), .out_5(main_12_out_5),
    .out_6(main_12_out_6), .out_7(main_12_out_7), .out_8(main_12_out_8));
  _7_Segment_Display u_7_segment_display_13 (
    .g(main_13_out_8), .f(main_13_out_3), .a(main_13_out_2), .b(main_13_out_7), .e(main_13_out_4),
    .d(main_13_out_5), .c(main_13_out_6));  // open: dp
  _2421_to_7_main main_13 (
    .in_1(in_8), .out_2(main_13_out_2), .out_3(main_13_out_3), .out_4(main_13_out_4), .out_5(main_13_out_5),
    .out_6(main_13_out_6), .out_7(main_13_out_7), .out_8(main_13_out_8));
endmodule
