// Logisim project 10 bcd down counter.circ as structural Verilog: 1 circuit, main circuit main
module main (
  input  in_1,
  input  \clock_신호 ,
  input  _1,
  input  _2,
  input  _3,
  input  _4,
  input  _5,
  input  _6,
  input  _7,
  input  _8,
  input  _9,
  output [3:0] out_12,
  output out_13
);

  wire and_1_out, and_2_out, and_3_out, and_4_out, and_5_out, j_k_ff_1_qn, j_k_ff_2_qn, j_k_ff_3_qn,
       or_1_out, or_2_out, or_3_out, or_4_out, or_5_out, or_6_out, or_7_out, or_9_out, Q2_Q1_out;

  J_K_Flip_Flop j_k_ff_1 (
    .J(1'b1), .clk(\clock_신호 ), .K(1'b1), .Q(out_12[0]), .Qn(j_k_ff_1_qn), .preset(or_1_out), .en(and_5_out),
    .reset(or_2_out));
  or or_1 (or_1_out, _1, _3, _5, _7, _9);
  or or_2 (or_2_out, _2, _4, _6, _8);
  J_K_Flip_Flop j_k_ff_2 (
    .J(and_1_out), .clk(\clock_신호 ), .K(j_k_ff_1_qn), .Q(out_12[1]), .Qn(j_k_ff_2_qn), .preset(or_3_out),
    .en(and_5_out), .reset(or_4_out));
  and and_1 (and_1_out, Q2_Q1_out, j_k_ff_1_qn);
  or or_3 (or_3_out, _2, _7, _3, _6);
  or or_4 (or_4_out, _1, _4, _5, _8, _9);
  and and_2 (and_2_out, j_k_ff_1_qn, out_12[3]);
  and and_3 (and_3_out, j_k_ff_2_qn, j_k_ff_1_qn);
  or Q2_Q1 (Q2_Q1_out, out_12[2], out_12[3]);
  or or_5 (or_5_out, _4, _5, _6, _7);
  J_K_Flip_Flop j_k_ff_3 (
    .J(and_2_out), .clk(\clock_신호 ), .K(and_3_out), .Q(out_12[2]), .Qn(j_k_ff_3_qn), .preset(or_5_out),
    .en(and_5_out), .reset(or_6_out));
  or or_6 (or_6_out, _1, _2, _3, _8, _9);
  and and_4 (and_4_out, j_k_ff_1_qn, j_k_ff_2_qn, j_k_ff_3_qn);
  J_K_Flip_Flop j_k_ff_4 (
    .J(and_4_out), .clk(\clock_신호 ), .K(j_k_ff_1_qn), .Q(out_12[3]), .preset(or_7_out), .en(and_5_out),
    .reset(or_9_out));  // open: Qn
  or or_7 (or_7_out, _8, _9);
  or or_8 (out_13, out_12[0], out_12[1], out_12[2], out_12[3]);
  or or_9 (or_9_out, _1, _2, _3, _4, _5, _6, _7);
  and and_5 (and_5_out, out_13, in_1);
endmodule
