// Logisim project SSD 구동회로 (E 포함).circ as structural Verilog: 1 circuit, main circuit main
module main (
  input  in_1,
  output out_2,
  output out_3,
  output out_4,
  output out_5,
  output out_6,
  output out_7,
  output out_8
);

  not not_1 (out_8, in_1);
  or or_1 (out_2, in_1, out_8);
  or or_2 (out_3, in_1, out_8);
  or or_3 (out_4, in_1, out_8);
  or or_4 (out_5, in_1, out_8);

  assign out_6 = in_1;
  assign out_7 = in_1;
endmodule
