// Logisim project SSD 구동회로 (d 포함).circ as structural Verilog: 1 circuit, main circuit main
module main (
  input  [3:0] in_1,
  input  in_2,
  output out_3,
  output out_4,
  output out_5,
  output out_6,
  output out_7,
  output out_8,
  output out_9
);

  wire _0_out, _1_out, _2_out, _3_out, _4_out, _5_out, _6_out, _7_out, _8_out, _9_out, not_1_out, not_2_out,
       not_3_out, not_4_out, not_5_out;

  not not_1 (not_1_out, in_2);
  not not_2 (not_2_out, in_1[3]);
  not not_3 (not_3_out, in_1[2]);
  not not_4 (not_4_out, in_1[1]);
  not not_5 (not_5_out, in_1[0]);
  and _9 (_9_out, not_4_out, in_1[3], not_3_out, in_2, in_1[0]);
  and _8 (_8_out, in_1[3], in_2, not_5_out, not_3_out, not_4_out);
  and _7 (_7_out, in_1[2], in_1[0], not_2_out, in_1[1], in_2);
  and _6 (_6_out, in_2, in_1[2], not_2_out, in_1[1], not_5_out);
  and _5 (_5_out, in_1[2], not_4_out, not_2_out, in_1[0], in_2);
  and _4 (_4_out, not_4_out, not_2_out, not_5_out, in_2, in_1[2]);
  and _3 (_3_out, not_3_out, not_2_out, in_1[1], in_2, in_1[0]);
  and _2 (_2_out, not_5_out, not_3_out, not_2_out, in_1[1], in_2);
  and _1 (_1_out, in_2, in_1[0], not_3_out, not_2_out, not_4_out);
  and _0 (_0_out, not_3_out, not_2_out, not_4_out, in_2, not_5_out);
  or a (out_3, _3_out, _9_out, _8_out, _7_out, _6_out, _5_out, _2_out, _0_out);
  or b (out_4, _9_out, _0_out, _6_out, _5_out, _7_out, _8_out, _4_out);
  or c (out_5, _8_out, _6_out, _2_out, not_1_out, _0_out);
  or d (out_6, _2_out, _9_out, _8_out, _6_out, _5_out, _3_out, _0_out, not_1_out);
  or e (out_7, _1_out, _4_out, _9_out, _8_out, _7_out, _6_out, _5_out, _3_out, _0_out, not_1_out);
  or f (out_8, not_1_out, _1_out, _9_out, _8_out, _7_out, _4_out, _3_out, _2_out, _0_out);
  or g (out_9, _3_out, _9_out, _8_out, _6_out, _5_out, _4_out, _2_out, not_1_out);
endmodule
