// Logisim project bcd down counter.circ as structural Verilog: 1 circuit, main circuit main
module main (
  input  \clock_신호 ,
  input  in_2,
  output [3:0] out_3,
  output \End_출력을_위한_00 ,
  output out_5
);

  wire and_1_out, and_2_out, and_3_out, and_4_out, j_k_ff_1_qn, j_k_ff_2_qn, j_k_ff_3_qn, not_1_out,
       Q2_Q1_out;

  not not_1 (not_1_out, in_2);
  nand nand_1 (\End_출력을_위한_00 , not_1_out, out_5);
  J_K_Flip_Flop j_k_ff_1 (
    .J(1'b1), .clk(\clock_신호 ), .K(1'b1), .Q(out_3[0]), .Qn(j_k_ff_1_qn), .en(\End_출력을_위한_00 ));  // open: preset, reset
  J_K_Flip_Flop j_k_ff_2 (
    .J(and_1_out), .clk(\clock_신호 ), .K(j_k_ff_1_qn), .Q(out_3[1]), .Qn(j_k_ff_2_qn), .en(\End_출력을_위한_00 ));  // open: preset, reset
  or Q2_Q1 (Q2_Q1_out, out_3[2], out_3[3]);
  and and_1 (and_1_out, Q2_Q1_out, j_k_ff_1_qn);
  and and_2 (and_2_out, j_k_ff_1_qn, out_3[3]);
  J_K_Flip_Flop j_k_ff_3 (
    .J(and_2_out), .clk(\clock_신호 ), .K(and_3_out), .Q(out_3[2]), .Qn(j_k_ff_3_qn), .en(\End_출력을_위한_00 ));  // open: preset, reset
  and and_3 (and_3_out, j_k_ff_2_qn, j_k_ff_1_qn);
  and and_4 (and_4_out, j_k_ff_1_qn, j_k_ff_2_qn, j_k_ff_3_qn);
  J_K_Flip_Flop j_k_ff_4 (
    .J(and_4_out), .clk(\clock_신호 ), .K(j_k_ff_1_qn), .Q(out_3[3]), .en(\End_출력을_위한_00 ));  // open: Qn, preset, reset
  nor nor_1 (out_5, out_3[3], out_3[2], out_3[1], out_3[0]);

  // Notes on the sheet:
  //   00인 경우
  //   en 비활성화
  //   십의 자리 숫자가 0인 경우
  //   모두 0인 경우 1
endmodule
