// Logisim project 십, 일의 자리 연결.circ as structural Verilog: 1 circuit, main circuit main
module main (
  input  in_1,
  input  in_2,
  input  in_3,
  input  in_4,
  input  in_5,
  input  in_6,
  input  in_7,
  input  in_8,
  input  in_9,
  input  in_10,
  output [3:0] \일의자리 ,
  output [3:0] \십의_자리 ,
  output out_13,
  output out_14,
  output out_15
);

  wire main_1_out_13, main_2_out_5;

  _10_bcd_down_counter_main main_1 (
    .out_12(\십의_자리 ), .\clock_신호 (in_1), ._1(in_2), ._2(in_3), ._3(in_5), ._4(in_8), ._5(in_10), ._6(in_9),
    ._7(in_7), ._8(in_6), ._9(in_4), .in_1(main_2_out_5), .out_13(main_1_out_13));
  bcd_down_counter_main main_2 (
    .out_3(\일의자리 ), .out_5(main_2_out_5), .in_2(main_1_out_13), .\clock_신호 (in_1), .\End_출력을_위한_00 (out_13));

  assign out_14 = out_13;
  assign out_15 = out_13;
endmodule
