// Logisim project 이게 메인입니다.circ as structural Verilog: 1 circuit, main circuit main
module main (
);

  wire _1_out, _2_out, _3_out, _4_out, _5_out, _6_out, _7_out, _8_out, _9_out, clock_1_out, main_1_out_2,
       main_1_out_3, main_1_out_4, main_1_out_5, main_1_out_6, main_1_out_7, main_1_out_8, main_2_out_3,
       main_2_out_4, main_2_out_5, main_2_out_6, main_2_out_7, main_2_out_8, main_2_out_9, main_3_out_3,
       main_3_out_4, main_3_out_5, main_3_out_6, main_3_out_7, main_3_out_8, main_3_out_9, main_4_out_13,
       main_4_out_14, main_4_out_15;
  wire [3:0] \main_4_십의_자리 , \main_4_일의자리 ;

  _7_Segment_Display u_7_segment_display_1 (
    .g(main_1_out_8), .f(main_1_out_3), .a(main_1_out_2), .b(main_1_out_7), .e(main_1_out_4),
    .d(main_1_out_5), .c(main_1_out_6));  // open: dp
  Clock clock_1 (.out(clock_1_out));
  Button _1 (.out(_1_out));
  \SSD_구동회로__E_포함__main  main_1 (
    .in_1(main_4_out_13), .out_2(main_1_out_2), .out_3(main_1_out_3), .out_4(main_1_out_4),
    .out_5(main_1_out_5), .out_6(main_1_out_6), .out_7(main_1_out_7), .out_8(main_1_out_8));
  _7_Segment_Display u_7_segment_display_2 (
    .g(main_3_out_9), .f(main_3_out_4), .a(main_3_out_3), .b(main_3_out_8), .e(main_3_out_5),
    .d(main_3_out_6), .c(main_3_out_7));  // open: dp
  Button _4 (.out(_4_out));
  Button _2 (.out(_2_out));
  Button _5 (.out(_5_out));
  Button _3 (.out(_3_out));
  \SSD_구동회로__d_포함__main  main_2 (
    .out_3(main_2_out_3), .out_4(main_2_out_4), .out_5(main_2_out_5), .out_6(main_2_out_6),
    .out_7(main_2_out_7), .out_8(main_2_out_8), .out_9(main_2_out_9), .in_1(\main_4_일의자리 ),
    .in_2(main_4_out_15));
  \SSD_구동회로__n_포함__main  main_3 (
    .out_3(main_3_out_3), .out_4(main_3_out_4), .out_5(main_3_out_5), .out_6(main_3_out_6),
    .out_7(main_3_out_7), .out_8(main_3_out_8), .out_9(main_3_out_9), .in_1(\main_4_십의_자리 ),
    .in_2(main_4_out_14));
  _7_Segment_Display u_7_segment_display_3 (
    .g(main_2_out_9), .f(main_2_out_4), .a(main_2_out_3), .b(main_2_out_8), .e(main_2_out_5),
    .d(main_2_out_6), .c(main_2_out_7));  // open: dp
  \십__일의_자리_연결_main  main_4 (
    .\일의자리 (\main_4_일의자리 ), .\십의_자리 (\main_4_십의_자리 ), .in_1(clock_1_out), .in_8(_4_out), .in_2(_1_out),
    .in_3(_2_out), .in_5(_3_out), .in_10(_5_out), .in_9(_6_out), .in_7(_7_out), .in_6(_8_out), .in_4(_9_out),
    .out_13(main_4_out_13), .out_14(main_4_out_14), .out_15(main_4_out_15));
  Button _7 (.out(_7_out));
  Button _9 (.out(_9_out));
  Button _6 (.out(_6_out));
  Button _8 (.out(_8_out));
endmodule
